# Fritzing sketch sketch (saved by Fritzing 0.9.3b)
breadboards: 1

parts:
  Mod1 = Arduino MKR Wifi 1010
  RHT1 = Humidity and Temperature Sensor RHT03

nets:
  N1: Mod1.D6, RHT1.Data-signal
  N2: Mod1.GND, RHT1.GND_1, RHT1.GND_2
  +5V: Mod1.+5V, RHT1.Vcc

custom parts:
  Arduino MKR Wifi 1010: Arduino MKR Wifi 1010, SAMD21 Cortex-M0+ 32bit Low Power ARM MCU,Flash Memory 256 KB, SRAM 32KB, 48mhz clock, Ublok Wifi interface.
